# Fritzing sketch attiny85-433-remote-switch (saved by Fritzing 0.9.3b)
circuit board: 2.91579cm x 3.81787cm
breadboards: 1
perfboards: 1

parts:
  Attin85 = attiny85 [package=dip]
  R1 = Resistor [tolerance=±5% resistance=4.7k package=THT]
  R3 = Resistor [tolerance=±5% resistance=220 package=THT]
  LED1 = LED - 5mm [color="Red (633nm)" package="5 mm [THT]"]
  R2 = Resistor [tolerance=±5% resistance=4.7k package=THT]
  R4 = Resistor [tolerance=±5% resistance=4.7k package=THT]
  Switch = molex pin header, 3 pins [form=molex]
  BC337 = NPN-Transistor [part_number=BC337 package="TO92 [THT]"]
  + = molex pin header, 2 pins [form=molex]
  RF433 = mystery part, 4 pins [chip_label=?]

nets:
  N1: Attin85.Pin_2, R4.Pin_0, Switch.pin1
  N2: Attin85.Pin_3, R2.Pin_0, Switch.pin2
  GND: Attin85.Pin_4, LED1.cathode, Switch.pin3, BC337.C, +.pin1
  N3: Attin85.Pin_5, R1.Pin_0
  N4: Attin85.Pin_6, R3.Pin_1
  N5: Attin85.Pin_7, RF433.pin2
  3.3V: Attin85.Pin_8, R2.Pin_1, R4.Pin_1, +.pin2, RF433.pin3
  N6: R1.Pin_1, BC337.B
  N7: R3.Pin_0, LED1.anode
  N8: BC337.E, RF433.pin4

// code stored in the sketch: attiny85-433-remote-switch.ino
#include <avr/sleep.h>
#include <avr/interrupt.h>
#include <x10rf.h>

#define senderPower 0
#define switchUp 3
#define switchDown 4
#define statusLED 1
#define tx 2
#define reps 2

volatile uint8_t portbhistory = 0xFF;
volatile boolean running = false;

x10rf myx10 = x10rf(tx, 0, reps);

void setup() {
  pinMode(switchUp, INPUT);
  pinMode(switchDown, INPUT);
  
  flash(true);
} // setup

void flash(boolean slow) {
  for (int k = 0; k < 10; k = k + 1) {
    if (k % 2 == 0) {
      digitalWrite(statusLED, HIGH);
    }
    else {
      digitalWrite(statusLED, LOW);
    }
    delay(slow ? 100 : 50);
  }
}

void sleep() {

  delay(500);
  // shutdown ports
  digitalWrite(statusLED, LOW);
  digitalWrite(senderPower, LOW);
  digitalWrite(tx, LOW);
  pinMode(senderPower, INPUT);
  pinMode(statusLED, INPUT);
  pinMode(tx, INPUT); // need to do this, otherwise RF consumes


//  set_sleep_mode(SLEEP_MODE_PWR_DOWN);  //festlegen des Schlafmoduses
//  sleep_enable();  //ermoeglichen der angegebenen Schlaffunktion
//  sleep_mode();  //starten der Schlaffunktion
//  //hier geht es nach dem Interrupt weiter
//  sleep_disable();  //deaktivieren der Schlaffunktion
//  power_all_enable();  //reaktivieren aller Chips/Funktionen

  GIMSK |= _BV(PCIE);                     // Enable Pin Change Interrupts
  PCMSK |= _BV(PCINT3);                   // Use PB3 as interrupt pin
  PCMSK |= _BV(PCINT4);                   // Use PB3 as interrupt pin
  ADCSRA &= ~_BV(ADEN);                   // ADC off
  set_sleep_mode(SLEEP_MODE_PWR_DOWN);    // replaces above statement
  sleep_enable();                         // Sets the Sleep Enable bit in the MCUCR Register (SE BIT)
  sei();                                  // Enable interrupts
  sleep_cpu();                            // sleep

  cli();                                  // Disable interrupts
  PCMSK &= ~_BV(PCINT3);
  PCMSK &= ~_BV(PCINT4);                  // Turn off interrupt
  sleep_disable();                        // Clear SE bit
  ADCSRA |= _BV(ADEN);                    // ADC on
  sei();                                  // Enable interrupts

  // enable ports
  pinMode(senderPower, OUTPUT);
  pinMode(statusLED, OUTPUT);
  pinMode(tx, OUTPUT);
  digitalWrite(senderPower, HIGH);
  myx10.begin();
  delay(100);
} // sleep


typedef enum { NONE, UP, DOWN } switchType;
volatile switchType button = NONE;


// found at https://sites.google.com/site/qeewiki/books/avr-guide/external-interrupts-on-the-atmega328

ISR(PCINT0_vect) {
  
  uint8_t changedbits;
  changedbits = PINB ^ portbhistory;

   if(changedbits & (1 << PB3)) {  
     button = UP;
   }
   if(changedbits & (1 << PB4)) {  
      button = DOWN;
   }

}

boolean isLongPress(int id) {
  int count = 0;
  while (digitalRead(id) == 0 && count < 6) {
    count++;
    delay(50);
  }
  return count > 5;
}

void loop() {
  sleep();
    
  switch (button) {
    case UP:
     if (isLongPress(switchUp)) {
      myx10.x10Switch('D', 15, ON);
      flash(true);
     } else {
      myx10.x10Switch('C', 15, ON);
      flash(false);
     }
     break;
   case DOWN:
     if (isLongPress(switchDown)) {
       myx10.x10Switch('D', 15, OFF); 
       flash(true);
     } else {
       myx10.x10Switch('C', 15, OFF);
       flash(false);
     }
     break;
   default:
     break;
  }
  

}
